# Fritzing sketch PennyAutoGarden (saved by Fritzing 0.9.3b)
breadboards: 2

parts:
  Part1 = Arduino Mega ADK (Rev3)
  5V_Output = RioRand LM2596
  A1 = 2 channel relay module [package=THT]
  A3 = 2 channel relay module [package=THT]
  L1 = Solenoid
  L2 = Solenoid
  L3 = Solenoid
  L5 = Solenoid
  L7 = Solenoid
  L8 = Solenoid
  L9 = Solenoid
  L10 = Solenoid
  L11 = Solenoid
  L298N2 = L298N DC motor driver
  L298N3 = L298N DC motor driver
  MH-ET_Live_Minikit_for_ESP1 = MH-ET Live Minikit for ESP32
  PS1 = prefix0000 [part_number=S-350-60]
  Part2 = Soil Moisture Sensor
  Part3 = Soil Moisture Sensor
  Part4 = Soil Moisture Sensor
  Part5 = Soil Moisture Sensor
  Part6 = Soil Moisture Sensor
  Part7 = Soil Moisture Sensor
  Part8 = Soil Moisture Sensor
  Part9 = Soil Moisture Sensor
  Part10 = Soil Moisture Sensor
  Part11 = Soil Moisture Sensor
  HC-SR04_Sensor_1 = HC-SR04 Ultrasonic Distance Sensor
  HC-SR04_Sensor_2 = HC-SR04 Ultrasonic Distance Sensor
  Part12 = BME280 Breakout
  F1 = Fan - Ventilador [package=THT]  # not connected
  S1 = PH meter [package=THT]
  Part13 = Soil Moisture Sensor
  S2 = PH meter [package=THT]
  J2 = 120V duplex outlet_1
  J3 = 120V duplex outlet_1
  L298N1 = L298N DC motor driver
  L6 = Solenoid
  DS1 = DS18B20 1-Wire Temperature Sensor Probe
  FloatValve = Round Pushbutton
  L12 = Solenoid
  F2 = Fan - Ventilador [package=THT]  # not connected
  F3 = Fan - Ventilador [package=THT]  # not connected
  F4 = Fan - Ventilador [package=THT]  # not connected
  F5 = Fan - Ventilador [package=THT]  # not connected
  F6 = Fan - Ventilador [package=THT]  # not connected
  F7 = Fan - Ventilador [package=THT]  # not connected
  J4 = 120V duplex outlet_1
  R1 = Resistor [tolerance=±5% resistance=220 package=THT]
  A2 = 2 channel relay module [package=THT]
  7V_Output = RioRand LM2596

nets:
  N1: Part1.A12, S2.pin1
  N2: Part1.A15, S1.pin1
  N3: Part1.A0, HC-SR04_Sensor_2.ECHO
  N4: Part1.A1, HC-SR04_Sensor_2.TRIG
  N5: Part1.A2, HC-SR04_Sensor_1.ECHO
  N6: Part1.A3, HC-SR04_Sensor_1.TRIG
  N7: Part1.GND, 7V_Output.Pin_4
  N8: Part1.VIN, 7V_Output.Pin_3
  N9: Part1.D0/RX0, MH-ET_Live_Minikit_for_ESP1.TXD
  N10: Part1.D1/TX0, MH-ET_Live_Minikit_for_ESP1.RXD
  N11: Part1.D22, A3.Pin_27
  N12: Part1.D24, A3.Pin_28
  N13: Part1.D25, Part13.SIG
  N14: Part1.D26, A3.Pin_29
  N15: Part1.D27, A1.Pin_27
  N16: Part1.D28, A3.Pin_30
  N17: Part1.D29, A1.Pin_28
  N18: Part1.D30, A2.Pin_30
  N19: Part1.D31, A1.Pin_29
  N20: Part1.D32, A2.Pin_29
  N21: Part1.D33, A1.Pin_30
  N22: Part1.D34, A2.Pin_28
  N23: Part1.D35, A2.Pin_27
  N24: Part1.D40, Part8.SIG
  N25: Part1.D41, Part10.SIG
  N26: Part1.D42, Part6.SIG
  N27: Part1.D43, Part2.SIG
  N28: Part1.D44, Part7.SIG
  N29: Part1.D45, Part3.SIG
  N30: Part1.D46, Part11.SIG
  N31: Part1.D47, Part5.SIG
  N32: Part1.D48, Part9.SIG
  N33: Part1.D49, Part4.SIG
  N34: 5V_Output.Pin_1, PS1.connector0, 7V_Output.Pin_1
  N35: 5V_Output.Pin_2, PS1.connector3, 7V_Output.Pin_2
  VCC: 5V_Output.Pin_3, L298N2.5V, L298N3.5V, Part2.VCC, Part3.VCC, Part4.VCC, Part5.VCC, Part6.VCC, Part7.VCC, Part8.VCC, Part9.VCC, Part10.VCC, Part11.VCC, HC-SR04_Sensor_1.VCC, HC-SR04_Sensor_2.VCC, L298N1.5V
  GND: 5V_Output.Pin_4, Part2.GND, Part3.GND, Part4.GND, Part5.GND, Part6.GND, Part7.GND, Part8.GND, Part9.GND, Part10.GND, Part11.GND, HC-SR04_Sensor_1.GND, HC-SR04_Sensor_2.GND, Part12.GND, FloatValve.leg1
  N36: A1.Pin_1, L5.pin2
  N37: A1.Pin_2, L5.pin1
  N38: A1.Pin_4, L3.pin2
  N39: A1.Pin_5, L3.pin1
  N40: A1.Pin_7, L12.pin2
  N41: A1.Pin_8, L12.pin1
  N42: A1.Pin_10, L2.pin2
  N43: A1.Pin_11, L2.pin1
  GND_2: A1.Pin_25, A3.Pin_25, MH-ET_Live_Minikit_for_ESP1.GND, S1.pin3, Part13.GND, S2.pin3, DS1.GND, A2.Pin_26
  VCC_2: A1.Pin_26, A3.Pin_26, MH-ET_Live_Minikit_for_ESP1.VCC, S1.pin2, Part13.VCC, S2.pin2, DS1.VDD, A2.Pin_25
  N44: A3.Pin_1, L1.pin2
  N45: A3.Pin_2, L1.pin1
  N46: A3.Pin_4, J3.G
  N47: A3.Pin_5, J3.H2
  N48: A3.Pin_7, J3.H1
  N49: A3.Pin_8, J3.N2
  N50: A3.Pin_9, J2.G
  N51: A3.Pin_10, J2.H2
  N52: L7.pin1, L298N1.OUT2
  N53: L7.pin2, L298N1.OUT1
  N54: L8.pin1, L298N2.OUT2
  N55: L8.pin2, L298N2.OUT1
  N56: L9.pin1, L298N2.OUT3
  N57: L9.pin2, L298N2.OUT4
  N58: L10.pin1, L298N3.OUT2
  N59: L10.pin2, L298N3.OUT1
  N60: L11.pin1, L298N3.OUT3
  N61: L11.pin2, L298N3.OUT4
  N62: L298N2.ENA, MH-ET_Live_Minikit_for_ESP1.IO33
  N63: L298N2.ENB, MH-ET_Live_Minikit_for_ESP1.IO35
  N64: L298N2.IN1, MH-ET_Live_Minikit_for_ESP1.IO19
  N65: L298N2.IN3, MH-ET_Live_Minikit_for_ESP1.IO18
  N66: L298N3.ENA, MH-ET_Live_Minikit_for_ESP1.IO4
  N67: L298N3.ENB, MH-ET_Live_Minikit_for_ESP1.TDI
  N68: L298N3.IN1, MH-ET_Live_Minikit_for_ESP1.IO16
  N69: L298N3.IN3, MH-ET_Live_Minikit_for_ESP1.IO17
  N70: MH-ET_Live_Minikit_for_ESP1.IO34, L298N1.ENB
  N71: MH-ET_Live_Minikit_for_ESP1.TMS, L298N1.ENA
  N72: MH-ET_Live_Minikit_for_ESP1.SVP, Part12.SCK/SCL
  N73: MH-ET_Live_Minikit_for_ESP1.IO26, Part12.SDI/SDA
  N74: MH-ET_Live_Minikit_for_ESP1.IO23, L298N1.IN1
  N75: MH-ET_Live_Minikit_for_ESP1.IO5, L298N1.IN3
  3.3V: MH-ET_Live_Minikit_for_ESP1.3.3V, Part12.3.3V, R1.Pin_1
  N76: MH-ET_Live_Minikit_for_ESP1.IO22, DS1.DQ, R1.Pin_0
  N77: MH-ET_Live_Minikit_for_ESP1.IO32, FloatValve.leg0
  N78: J2.H1, A2.Pin_4
  N79: L298N1.OUT3, L6.pin1
  N80: L298N1.OUT4, L6.pin2
  N81: J4.G, A2.Pin_7
  N82: J4.N2, A2.Pin_8

custom parts:
  2 channel relay module: 4 channel Relay Module 5V 12V 24V High and Low Level Trigger Relay Control With Optocoupler Two Way relays DC 5 V 12 V 24 V Volt.
  L298N DC motor driver: 2x DC motor driver with 78M05 positive voltage regulator (7..35 V) L298N: max 46 V, 2 A Set 5 V Enable jumper to enable 5 V regultor (needed for the L298N) and +5 V output at screw terminal or supply external +5 V at screw terminal Set ENA and/or ENB to +5 V to enable motor permanently or supply ENA and/or ENB with PWM signal IN1 and IN2 set rotation directory for motor A (OUT1/OUT2) IN2 and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
  MH-ET Live Minikit for ESP32: MH-ET Live Minikit for ESP32 ( http://mh.nodebb.com/topic/8/mh-et-live-minikit-for-esp32/2/) PCB footprint is invalid.
  Fan - Ventilador: Ventilador de 2 pines, se encuentra comunmente en computadoras de escritorio
  120V duplex outlet_1: 120V duplex outlet.
