# Fritzing sketch PennyAutoGardenrewire (saved by Fritzing 0.9.3b)
breadboards: 2

parts:
  Part1 = Arduino Mega ADK (Rev3)  # not connected
  5V_Output = RioRand LM2596
  A1 = 2 channel relay module [package=THT]  # not connected
  A3 = 2 channel relay module [package=THT]  # not connected
  L1 = Solenoid  # not connected
  L2 = Solenoid  # not connected
  L3 = Solenoid  # not connected
  L5 = Solenoid  # not connected
  L7 = Solenoid  # not connected
  L8 = Solenoid  # not connected
  L9 = Solenoid  # not connected
  L10 = Solenoid  # not connected
  L11 = Solenoid  # not connected
  L298N2 = L298N DC motor driver
  L298N3 = L298N DC motor driver
  MH-ET_Live_Minikit_for_ESP1 = MH-ET Live Minikit for ESP32
  PS1 = prefix0000 [part_number=S-350-60]
  Part2 = Soil Moisture Sensor  # not connected
  Part3 = Soil Moisture Sensor  # not connected
  Part4 = Soil Moisture Sensor  # not connected
  Part5 = Soil Moisture Sensor  # not connected
  Part6 = Soil Moisture Sensor  # not connected
  Part7 = Soil Moisture Sensor  # not connected
  Part8 = Soil Moisture Sensor  # not connected
  Part9 = Soil Moisture Sensor  # not connected
  Part10 = Soil Moisture Sensor  # not connected
  Part11 = Soil Moisture Sensor  # not connected
  HC-SR04_Sensor_1 = HC-SR04 Ultrasonic Distance Sensor  # not connected
  HC-SR04_Sensor_2 = HC-SR04 Ultrasonic Distance Sensor  # not connected
  Part12 = BME280 Breakout  # not connected
  F1 = Fan - Ventilador [package=THT]  # not connected
  S1 = PH meter [package=THT]  # not connected
  Part13 = Soil Moisture Sensor  # not connected
  S2 = PH meter [package=THT]  # not connected
  J2 = 120V duplex outlet_1  # not connected
  J3 = 120V duplex outlet_1  # not connected
  L298N1 = L298N DC motor driver
  L6 = Solenoid  # not connected
  DS1 = DS18B20 1-Wire Temperature Sensor Probe  # not connected
  FloatValve = Round Pushbutton  # not connected
  L12 = Solenoid  # not connected
  F2 = Fan - Ventilador [package=THT]
  F3 = Fan - Ventilador [package=THT]
  F4 = Fan - Ventilador [package=THT]
  F5 = Fan - Ventilador [package=THT]
  F6 = Fan - Ventilador [package=THT]
  F7 = Fan - Ventilador [package=THT]
  J4 = 120V duplex outlet_1  # not connected
  R1 = Resistor [tolerance=±5% resistance=220 package=THT]  # not connected
  A2 = 2 channel relay module [package=THT]  # not connected
  7V_Output = RioRand LM2596
  J5 = longpad pin header, 18 pins [form="long pad"]
  J6 = longpad pin header, 18 pins [form="long pad"]
  J9 = longpad pin header, 7 pins [form="long pad"]
  J8 = longpad pin header, 7 pins [form="long pad"]

nets:
  N1: 5V_Output.Pin_1, J5.pin3
  N2: 5V_Output.Pin_2, J6.pin2
  5V: 5V_Output.Pin_3, L298N2.5V, L298N3.5V, MH-ET_Live_Minikit_for_ESP1.VCC, L298N1.5V
  N3: 5V_Output.Pin_4, MH-ET_Live_Minikit_for_ESP1.GND
  12V: L298N3.12V, L298N1.12V
  GND: L298N3.GND, L298N1.GND
  N4: PS1.connector2, J6.pin1
  N5: PS1.connector4, J5.pin1
  N6: F2.5V, J9.pin1
  N7: F2.GND, J8.pin1
  N8: F3.5V, J9.pin3
  N9: F3.GND, J8.pin3
  N10: F4.5V, J9.pin5
  N11: F4.GND, J8.pin5
  N12: F5.5V, J9.pin2
  N13: F5.GND, J8.pin2
  N14: F6.5V, J9.pin4
  N15: F6.GND, J8.pin4
  N16: F7.5V, J9.pin6
  N17: F7.GND, J8.pin6
  N18: 7V_Output.Pin_1, J5.pin2
  N19: 7V_Output.Pin_2, J6.pin3
  N20: J6.pin18, J9.pin7

custom parts:
  2 channel relay module: 4 channel Relay Module 5V 12V 24V High and Low Level Trigger Relay Control With Optocoupler Two Way relays DC 5 V 12 V 24 V Volt.
  L298N DC motor driver: 2x DC motor driver with 78M05 positive voltage regulator (7..35 V) L298N: max 46 V, 2 A Set 5 V Enable jumper to enable 5 V regultor (needed for the L298N) and +5 V output at screw terminal or supply external +5 V at screw terminal Set ENA and/or ENB to +5 V to enable motor permanently or supply ENA and/or ENB with PWM signal IN1 and IN2 set rotation directory for motor A (OUT1/OUT2) IN2 and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
  MH-ET Live Minikit for ESP32: MH-ET Live Minikit for ESP32 ( http://mh.nodebb.com/topic/8/mh-et-live-minikit-for-esp32/2/) PCB footprint is invalid.
  Fan - Ventilador: Ventilador de 2 pines, se encuentra comunmente en computadoras de escritorio
  120V duplex outlet_1: 120V duplex outlet.
